# Fritzing sketch NRF24L01 (saved by Fritzing 0.9.3b)
circuit board: 8.46667cm x 5.64444cm
breadboards: 1

parts:
  Part1 = Arduino Nano (Rev3.0)
  Part2 = NRF24L01+ Breakout Board
  R1 = Resistor [tolerance=±5% resistance=220 package=THT]
  R2 = Resistor [tolerance=±5% resistance=220 package=THT]
  J1 = Basic Servo
  J2 = Basic Servo
  J3 = Basic Servo
  J4 = Basic Servo
  JP1 = Header 1 [package=smtso-256-et]
  JP2 = Header 1 [package=smtso-256-et]

nets:
  GND: Part1.GND, Part2.GND
  N1: Part1.D2, J1.pulse
  N2: Part1.D3, J2.pulse
  N3: Part1.D4, J3.pulse
  N4: Part1.D5, J4.pulse
  N5: Part1.D9, Part2.CE
  N6: Part1.D10, Part2.CS
  N7: Part1.D11/MOSI, Part2.MOSI
  N8: Part1.D12/MISO, Part2.MISO
  N9: Part1.3V3, R2.Pin_1
  N10: Part1.D13/SCK, R1.Pin_1
  N11: Part2.VCC, R2.Pin_0
  N12: Part2.SCK, R1.Pin_0
  GND_2: J1.gnd, J2.gnd, J4.gnd, JP1.1
  VCC: J1.vcc, J2.vcc, J3.vcc, J4.vcc, JP2.1
