# Fritzing sketch Rx (saved by Fritzing 0.9.3b)

parts:
  Arduino_Nano = Arduino Nano (Rev3.0)
  U1 = LIPO-1000mAh [package=lipo-1000]
  U2 = LIPO-1000mAh [package=lipo-1000]
  Reed_Switch = Reed switch [package=THT]
  Middle_Body = Basic Servo
  Posterior_Body = Basic Servo
  Caudal_Fin = Basic Servo
  LM2596_Buck_Converter = RioRand LM2596
  NRF24L01 = NRF24L01+ Breakout Board
  C1 = Electrolytic Capacitor [capacitance=10µF package="100 mil [THT, electrolytic]"]
  C2 = Ceramic Capacitor [capacitance=100nF package="100 mil [THT, multilayer]"]

nets:
  GND: Arduino_Nano.GND, U2.-, Middle_Body.gnd, Posterior_Body.gnd, LM2596_Buck_Converter.Pin_2, LM2596_Buck_Converter.Pin_4, NRF24L01.GND, C1.-, C2.1
  N1: Arduino_Nano.D2, Caudal_Fin.pulse
  N2: Arduino_Nano.D3, Posterior_Body.pulse
  N3: Arduino_Nano.D4, Middle_Body.pulse
  N4: Arduino_Nano.D9, NRF24L01.CE
  N5: Arduino_Nano.D10, NRF24L01.CS
  N6: Arduino_Nano.D11/MOSI, NRF24L01.MOSI
  N7: Arduino_Nano.D12/MISO, NRF24L01.MISO
  N8: Arduino_Nano.VIN, Reed_Switch.pin_2, LM2596_Buck_Converter.Pin_1
  3V3: Arduino_Nano.3V3, NRF24L01.VCC, C1.+, C2.0
  N9: Arduino_Nano.D13/SCK, NRF24L01.SCK
  N10: U1.+, Reed_Switch.pin_1
  N11: U1.-, U2.+
  N12: Middle_Body.vcc, LM2596_Buck_Converter.Pin_3
