# Fritzing sketch Battery_Charger_Ciruit (saved by Fritzing 0.9.3b)

parts:
  Input = USB_MICROB_PLUG [package=micro-b-ra-th]
  To_Nano = USB Connectors [package=usb-a-s-nosilk]
  Battery_Charger_Vcc/GND = female pin header, 2 pins [form="♀ (female)"]
  IN+ = Header 1 [package=1x01_offset]
  IN+_2 = Header 1 [package=1x01_offset]
  IN- = Header 1 [package=1x01_offset]
  IN-_2 = Header 1 [package=1x01_offset]
  GND = Header 1 [package=1x01_offset]
  VCC = Header 1 [package=1x01_offset]
  D1 = Rectifier Diode [package="Melf DO-213 AA [SMD]"]
  IN+_3 = TP4056 [chip_label=TP4056 package="DIP (Dual Inline) [THT]"]
  IN-_3 = TP4056 [chip_label=TP4056 package="DIP (Dual Inline) [THT]"]
  S1 = SWITCH-MOMENTARY-2 [package=reed_switch_pth]
  OUT+ = LIPO-1000mAh [package=lipo-1000]
  OUT- = LIPO-1000mAh [package=lipo-1000]
  IN-_4 = Rectifier Diode [package="Melf DO-213 AA [SMD]"]
  IN-_5 = Rectifier Diode [package="Melf DO-213 AA [SMD]"]

nets:
  N1: Input.VCC, To_Nano.VBUS, Battery_Charger_Vcc/GND.pin2
  N2: Input.D-, To_Nano.D-
  N3: Input.D+, To_Nano.D+
  GND: Input.GND, To_Nano.GND, Battery_Charger_Vcc/GND.pin1
  N4: IN+.1, IN+_2.1, D1.cathode
  N5: IN-.1, IN-_2.1, GND.1
  N6: VCC.1, D1.anode
  N7: IN+_3.pin2, IN-_4.anode
  N8: IN+_3.pin4, OUT+.+
  N9: IN+_3.pin5, OUT+.-
  N10: IN+_3.pin6, S1.1
  N11: IN-_3.pin2, IN-_5.anode
  N12: IN-_3.pin3, S1.2
  N13: IN-_3.pin4, OUT-.+
  N14: IN-_3.pin5, OUT-.-

custom parts:
  TP4056: A DIP stand-in part for whatever IC you want. With 6 pins on a 300mil dual inline package (DIP) footprint.
