# Fritzing sketch Tx (saved by Fritzing 0.9.3b)

parts:
  Arduino_Nano = Arduino Nano (Rev3.0)
  NRF24L01 = NRF24L01+ Breakout Board
  C3 = Electrolytic Capacitor [capacitance=10µF package="100 mil [THT, electrolytic]"]
  C4 = Ceramic Capacitor [capacitance=100nF package="100 mil [THT, multilayer]"]
  Joystick_Direction_Control_(Forward/Backward) = Thumb Joystick
  SPST_Switch = SWITCH_SPDT [package=kps-1290]
  Joystick_Direction_(Left/Right) = Thumb Joystick
  U1 = LIPO-1000mAh [package=lipo-1000]
  U2 = LIPO-1000mAh [package=lipo-1000]
  RGB_LED = RGB LED (com. anode, rbg) [package="5 mm [THT]"]

nets:
  GND: Arduino_Nano.RESET, Arduino_Nano.GND, NRF24L01.GND, C3.-, C4.1, Joystick_Direction_Control_(Forward/Backward).GND
  N1: Arduino_Nano.D2, Joystick_Direction_Control_(Forward/Backward).SEL
  N2: Arduino_Nano.D3, Joystick_Direction_(Left/Right).SEL
  N3: Arduino_Nano.D4, RGB_LED.green_cathode
  N4: Arduino_Nano.D5, RGB_LED.blue_cathode
  N5: Arduino_Nano.D6, RGB_LED.red_cathode
  N6: Arduino_Nano.D9, NRF24L01.CE
  N7: Arduino_Nano.D10, NRF24L01.CS
  N8: Arduino_Nano.D11/MOSI, NRF24L01.MOSI
  N9: Arduino_Nano.D12/MISO, NRF24L01.MISO
  N10: Arduino_Nano.VIN, SPST_Switch.S
  VCC: Arduino_Nano.5V, Joystick_Direction_Control_(Forward/Backward).VCC, Joystick_Direction_(Left/Right).VCC, RGB_LED.common_anode
  N11: Arduino_Nano.A3, Joystick_Direction_(Left/Right).VERT
  N12: Arduino_Nano.A2, Joystick_Direction_(Left/Right).HORZ
  N13: Arduino_Nano.A1, Joystick_Direction_Control_(Forward/Backward).VERT
  N14: Arduino_Nano.A0, Joystick_Direction_Control_(Forward/Backward).HORZ
  3V3: Arduino_Nano.3V3, NRF24L01.VCC, C3.+, C4.0
  N15: Arduino_Nano.D13/SCK, NRF24L01.SCK
  N16: SPST_Switch.P, U1.+
  N17: U1.-, U2.+
